// Logisim project progetto-architettura.circ as structural Verilog: 5 circuits, main circuit main
module main (
);

  wire Clock, random_starting_car_1_enable_random, random_starting_car_2_enable_random;
  wire [5:0] bit_extender_1_out, bit_extender_2_out;
  wire [7:0] random_1_out, random_2_out;
  wire [19:0] car_1_car_representation, random_starting_car_1_car, random_starting_car_2_car;

  Clock clock_1 (.out(Clock));
  Random #(.seed(424242)) random_1 (.clk(random_starting_car_1_enable_random), .out(random_1_out));  // open: next, clr
  Random #(.seed(828282)) random_2 (.clk(random_starting_car_2_enable_random), .out(random_2_out));  // open: next, clr
  Bit_Extender #(.out_width(6)) bit_extender_1 (.in(random_1_out), .out(bit_extender_1_out));
  Bit_Extender #(.out_width(6)) bit_extender_2 (.in(random_2_out), .out(bit_extender_2_out));
  DotMatrix #(.matrixcols(16), .matrixrows(20)) dotmatrix_1 (
    .col0({20{1'b0}}), .col1(random_starting_car_1_car), .col2(random_starting_car_1_car), .col3({20{1'b0}}),
    .col4(random_starting_car_2_car), .col5(random_starting_car_2_car), .col6({20{1'b0}}), .col7(20'h739ce),
    .col8({20{1'b0}}), .col9(car_1_car_representation), .col10(car_1_car_representation), .col11({20{1'b0}}),
    .col12(20'h3efba), .col13(20'h22a2a), .col14(20'h2efae), .col15({20{1'b0}}));
  random_starting_car random_starting_car_1 (
    .car(random_starting_car_1_car), .enable_random(random_starting_car_1_enable_random),
    .random_number(bit_extender_1_out), .clock(Clock));
  random_starting_car random_starting_car_2 (
    .car(random_starting_car_2_car), .enable_random(random_starting_car_2_enable_random),
    .random_number(bit_extender_2_out), .clock(Clock));
  car car_1 (
    .can_proceed(1'b1), .clock(Clock), .car_representation(car_1_car_representation));  // open: is_car_out_of_sight

  // Notes on the sheet:
  //   bug noto: quando il random arriva a 0 non cambia piu'
endmodule

module count_to_three (
  input  reset,
  input  clock,
  output is_less_than_three
);

  wire and_1_out, and_2_out, and_3_out, comparator_1_eq, comparator_1_gt, comparator_1_lt;
  wire [2:0] adder_1_out, d_ff_1_q;

  D_Flip_Flop d_ff_1 (.clk(clock), .D(and_1_out), .Q(d_ff_1_q[0]));  // open: Qn, preset, en, reset
  and and_1 (and_1_out, adder_1_out[0], ~reset);  // AND_Gate
  D_Flip_Flop d_ff_2 (.clk(clock), .D(and_2_out), .Q(d_ff_1_q[1]));  // open: Qn, preset, en, reset
  and and_2 (and_2_out, adder_1_out[1], ~reset);  // AND_Gate
  D_Flip_Flop d_ff_3 (.clk(clock), .D(and_3_out), .Q(d_ff_1_q[2]));  // open: Qn, preset, en, reset
  and and_3 (and_3_out, adder_1_out[2], ~reset);  // AND_Gate
  Comparator #(.width(3)) comparator_1 (
    .a(d_ff_1_q), .b(3'b011), .gt(comparator_1_gt), .eq(comparator_1_eq), .lt(comparator_1_lt));
  Multiplexer #(.select(2)) multiplexer_1 (
    .in0(comparator_1_gt), .in1(comparator_1_eq), .in2(comparator_1_lt), .out(is_less_than_three), .sel(2'b10));  // open: in3, en
  Adder #(.width(3)) adder_1 (.a(d_ff_1_q), .b({2'b00, is_less_than_three}), .out(adder_1_out));  // open: cin, cout

  // Notes on the sheet:
  //   Counts up to 3, reset clears the memory
  //   Outputs 1 until the value stored in memory is less or equal than 3, 0 otherwise
endmodule

module car (
  input  clock,
  input  can_proceed,
  output [19:0] car_representation,
  output is_car_out_of_sight
);

  wire count_to_three_1_is_less_than_three;

  count_to_three count_to_three_1 (
    .reset(is_car_out_of_sight), .clock(clock), .is_less_than_three(count_to_three_1_is_less_than_three));
  Shift_Register #(.length(20)) shift_register_1 (
    .shift(can_proceed), .in(count_to_three_1_is_less_than_three), .clk(clock), .q0(car_representation[19]),
    .q1(car_representation[18]), .q2(car_representation[17]), .q3(car_representation[16]),
    .q4(car_representation[15]), .q5(car_representation[14]), .q6(car_representation[13]),
    .q7(car_representation[12]), .q8(car_representation[11]), .q9(car_representation[10]),
    .q10(car_representation[9]), .q11(car_representation[8]), .q12(car_representation[7]),
    .q13(car_representation[6]), .q14(car_representation[5]), .q15(car_representation[4]),
    .q16(car_representation[3]), .q17(car_representation[2]), .q18(car_representation[1]),
    .q19(car_representation[0]));  // open: out, load, clr, d0, d1, d2, d3, d4, d5, d6, d7, d8, d9, d10, d11, d12, d13, d14, d15, d16, d17, d18, d19
  Comparator #(.width(20)) comparator_1 (
    .a(car_representation), .b({20{1'b0}}), .eq(is_car_out_of_sight));  // open: gt, lt
  D_Flip_Flop d_ff_1 ();  // open: clk, D, Q, Qn, preset, en, reset
  D_Flip_Flop d_ff_2 ();  // open: clk, D, Q, Qn, preset, en, reset
  D_Flip_Flop d_ff_3 ();  // open: clk, D, Q, Qn, preset, en, reset

  // Notes on the sheet:
  //   Represents (half) a car that advances in space
  //   Outputs 1) the representation of (half) a car as series of 1s, and 2) 1 when  it's out of sight
endmodule

module random_starting_car (
  input  clock,
  input  [5:0] random_number,
  output enable_random,
  output [19:0] car
);

  wire car_1_is_car_out_of_sight, counter_with_reset_1_is_running, counter_with_reset_2_is_running,
       not_2_out, or_1_out, should_reset_counter;
  wire [7:0] bit_extender_1_out;

  counter_with_reset counter_with_reset_1 (
    .clear(should_reset_counter), .max_value(8'h18), .can_proceed(clock), .clock(clock),
    .is_running(counter_with_reset_1_is_running));  // open: current_value
  or or_1 (or_1_out, counter_with_reset_1_is_running, not_2_out);
  car car_1 (
    .can_proceed(or_1_out), .clock(clock), .car_representation(car),
    .is_car_out_of_sight(car_1_is_car_out_of_sight));
  not not_1 (enable_random, counter_with_reset_1_is_running);
  not not_2 (not_2_out, counter_with_reset_2_is_running);
  and and_1 (should_reset_counter, car_1_is_car_out_of_sight, not_2_out);
  assign bit_extender_1_out = {{2{1'b0}}, random_number};  // Bit_Extender bit_extender_1
  counter_with_reset counter_with_reset_2 (
    .clear(counter_with_reset_1_is_running), .max_value(bit_extender_1_out), .can_proceed(enable_random),
    .clock(clock), .is_running(counter_with_reset_2_is_running));  // open: current_value
endmodule

module counter_with_reset (
  input  clear,
  input  [7:0] max_value,
  input  can_proceed,
  input  clock,
  output is_running,
  output [7:0] current_value
);

  wire and_1_out, comparator_1_eq, multiplexer_1_out;
  wire [7:0] adder_1_out, bit_extender_1_out;

  and and_1 (and_1_out, can_proceed, clock);
  Register register_1 (.D(adder_1_out), .en(1'b1), .Q(current_value), .clk(and_1_out), .clr(clear));
  Comparator comparator_1 (.a(current_value), .b(max_value), .eq(comparator_1_eq), .lt(is_running));  // open: gt
  Multiplexer #(.select(2)) multiplexer_1 (
    .in1(comparator_1_eq), .in2(is_running), .out(multiplexer_1_out), .sel(2'b10));  // open: in0, in3, en
  assign bit_extender_1_out = {{7{1'b0}}, multiplexer_1_out};  // Bit_Extender bit_extender_1
  Adder adder_1 (.a(current_value), .b(bit_extender_1_out), .out(adder_1_out));  // open: cin, cout
endmodule
